# Fritzing sketch ATX Power Control (saved by Fritzing 0.9.3b)
circuit board: 8.46667cm x 5.64444cm
breadboards: 1

parts:
  Arduino = Arduino Uno (Rev3)
  J2 = screw terminal, 6 pins
  Combined_LED_PB = Round Pushbutton
  LED1 = LED - 5mm [color="Red (633nm)" package="5 mm [THT]"]
  R2 = Resistor [tolerance=±5% resistance=220 package=THT]

nets:
  N1: Arduino.D12/MISO, LED1.cathode
  N2: Arduino.D13/SCK, Combined_LED_PB.leg0
  N3: Arduino.GND, J2.pin3, Combined_LED_PB.leg1, R2.Pin_0
  N4: Arduino.D2, J2.pin1
  N5: Arduino.VIN, J2.pin2
  N6: LED1.anode, R2.Pin_1
