# Fritzing sketch Audio Controller (saved by Fritzing 0.9.3b)
circuit board: 8.46667cm x 5.64444cm
breadboards: 1

parts:
  Part1 = Arduino Mega 2560 (Rev3)
  POWER = Screw terminal - 2 pins [package=THT]
  128x64_I2C_OLED = Grove OLED 128x96
  R-BACK = Resistor [tolerance=±5% resistance=10k package=THT]
  B-UP = Pushbutton [package="[THT]"]
  B-DOWN = Pushbutton [package="[THT]"]
  B-BACK = Pushbutton [package="[THT]"]
  B-SEL = Pushbutton [package="[THT]"]
  R-SEL = Resistor [tolerance=±5% resistance=10k package=THT]
  R-DOWN = Resistor [tolerance=±5% resistance=10k package=THT]
  R-UP = Resistor [tolerance=±5% resistance=10k package=THT]
  I2C_BUS = Screw terminal - 2 pins [package=THT]

nets (from the breadboard view):
  N1: Part1.D21/SCL, 128x64_I2C_OLED.SCL, I2C_BUS.pin2
  N2: Part1.D20/SDA, 128x64_I2C_OLED.SDA, I2C_BUS.pin1
  GND: Part1.GND, POWER.pin2, 128x64_I2C_OLED.GND, R-BACK.Pin_1, R-SEL.Pin_1, R-DOWN.Pin_1, R-UP.Pin_1
  VIN: Part1.VIN, POWER.pin1, 128x64_I2C_OLED.VCC, B-UP.Pin_1, B-UP.Pin_2, B-DOWN.Pin_1, B-DOWN.Pin_2, B-BACK.Pin_1, B-BACK.Pin_2, B-SEL.Pin_3, B-SEL.Pin_4
  N3: Part1.D22, B-SEL.Pin_1, B-SEL.Pin_2, R-SEL.Pin_0
  N4: Part1.D24, R-BACK.Pin_0, B-BACK.Pin_3, B-BACK.Pin_4
  N5: Part1.D26, B-UP.Pin_3, B-UP.Pin_4, R-UP.Pin_0
  N6: Part1.D28, B-DOWN.Pin_3, B-DOWN.Pin_4, R-DOWN.Pin_0

notes:
  I2C BUS
  Out to VU Analyser
