# Fritzing sketch RTC Issue (saved by Fritzing 0.9.3b)
breadboards: 1

parts:
  Part1 = Arduino Uno (Rev3)
  Part2 = Arduino Mega 2560 (Rev3)
  Part3 = Real Time Clock Module - DS1307 RTC Breakout Board
  Part4 = Real Time Clock Module - DS1307 RTC Breakout Board
  5V_Power_Rail = Power Jack [package=power_jack_pth]

nets:
  N1: Part1.A4/SDA, Part3.SDA
  N2: Part1.A5/SCL, Part3.SCL
  GND: Part1.GND, Part2.GND, Part3.GND, Part4.GND, 5V_Power_Rail.GND
  5V: Part1.5V, Part3.5V
  VIN: Part1.VIN, Part2.VIN, 5V_Power_Rail.PWR
  N3: Part2.D21/SCL, Part4.SCL
  N4: Part2.D20/SDA, Part4.SDA
  5V_2: Part2.5V, Part4.5V
