# Fritzing sketch VU Analyser Pair (saved by Fritzing 0.9.3b)
circuit board: 8.46667cm x 5.64444cm
breadboards: 1

parts:
  CAP-R1 = Ceramic Capacitor [capacitance=100nF package="100 mil [THT, multilayer]"]
  RL1-5K = Resistor [tolerance=±5% resistance=4.7k package=THT]
  RR1-5K = Resistor [tolerance=±5% resistance=4.7k package=THT]
  RL2-5K = Resistor [tolerance=±5% resistance=4.7k package=THT]
  RL1-100K = Resistor [tolerance=±5% resistance=100k package=THT]
  RR1-100K = Resistor [tolerance=±5% resistance=100k package=THT]
  RL2-100K = Resistor [tolerance=±5% resistance=100k package=THT]
  RR2-100K = Resistor [tolerance=±5% resistance=100k package=THT]
  CAP-L1 = Ceramic Capacitor [capacitance=100nF package="100 mil [THT, multilayer]"]
  AUDIO_INPUT = Audio Jack (TRS) 3.5mm [package="4Ucon 08780 [THT]"]
  POWER = Screw terminal - 2 pins [package=THT]
  I2C = Screw terminal - 2 pins [package=THT]
  J14 = female pin header, 2 pins [form="♀ (female)"]
  J15 = female pin header, 2 pins [form="♀ (female)"]
  J16 = female pin header, 8 pins [form="♀ (female)"]  # not connected
  J17 = female pin header, 8 pins [form="♀ (female)"]  # not connected
  J2 = female pin header, 8 pins [form="♀ (female)"]
  GND = female pin header, 2 pins [form="♀ (female)"]
  +5V = female pin header, 2 pins [form="♀ (female)"]
  Arduino_Nano = Arduino Nano (Rev3.0)
  RR2-5K = Resistor [tolerance=±5% resistance=4.7k package=THT]
  GND_2 = female pin header, 2 pins [form="♀ (female)"]
  +5V_2 = female pin header, 2 pins [form="♀ (female)"]
  J6 = female pin header, 3 pins [form="♀ (female)"]
  J7 = female pin header, 1 pin [form="♀ (female)"]
  J8 = female pin header, 1 pin [form="♀ (female)"]
  J9 = female pin header, 3 pins [form="♀ (female)"]
  J10 = female pin header, 4 pins [form="♀ (female)"]
  J12 = female pin header, 15 pins [form="♀ (female)"]
  J5 = female pin header, 4 pins [form="♀ (female)"]
  J13 = female pin header, 15 pins [form="♀ (female)"]
  Arduino_Nano_2 = Arduino Nano (Rev3.0)
  J3 = female pin header, 8 pins [form="♀ (female)"]

nets:
  N1: CAP-R1.0, AUDIO_INPUT.Tip
  N2: CAP-R1.1, RR1-5K.Pin_0
  N3: RL1-5K.Pin_0, CAP-L1.1
  N4: RL1-5K.Pin_1, RL1-100K.Pin_1, RL2-100K.Pin_0, Arduino_Nano.A0
  N5: RR1-5K.Pin_1, RR1-100K.Pin_1, RR2-100K.Pin_0, Arduino_Nano_2.A0
  N6: RL2-5K.Pin_0, Arduino_Nano.3V3
  N7: RL2-5K.Pin_1, RL2-100K.Pin_1, Arduino_Nano.AREF
  GND: RL1-100K.Pin_0, RR1-100K.Pin_0, AUDIO_INPUT.Sleeve, POWER.pin2, J14.pin1, J15.pin1, GND.pin1, GND.pin2, Arduino_Nano.GND, GND_2.pin1, GND_2.pin2, J12.pin4, J13.pin4, Arduino_Nano_2.GND
  N8: RR2-100K.Pin_1, RR2-5K.Pin_0, Arduino_Nano_2.AREF
  N9: CAP-L1.0, AUDIO_INPUT.Ring
  VIN: POWER.pin1, J14.pin2, J15.pin2, +5V.pin1, +5V.pin2, Arduino_Nano.VIN, +5V_2.pin1, +5V_2.pin2, Arduino_Nano_2.VIN
  N10: I2C.pin1, Arduino_Nano.A5, Arduino_Nano_2.A5
  N11: I2C.pin2, Arduino_Nano.A4, Arduino_Nano_2.A4
  N12: J2.pin1, Arduino_Nano.D3, J13.pin6
  N13: J2.pin2, Arduino_Nano.D4, J13.pin7
  N14: J2.pin3, Arduino_Nano.D5, J13.pin8
  N15: J2.pin4, Arduino_Nano.D6, J13.pin9
  N16: J2.pin5, Arduino_Nano.D7, J13.pin10
  N17: J2.pin6, Arduino_Nano.D8, J13.pin11
  N18: J2.pin7, Arduino_Nano.D9, J13.pin12
  N19: J2.pin8, Arduino_Nano.D10, J13.pin13
  N20: Arduino_Nano.D1/TX, J13.pin1
  N21: Arduino_Nano.D0/RX, J13.pin2
  N22: Arduino_Nano.RESET, J10.pin1, J13.pin3
  N23: Arduino_Nano.D2, J13.pin5
  N24: Arduino_Nano.D11/MOSI, J13.pin14
  N25: Arduino_Nano.D12/MISO, J13.pin15
  N26: Arduino_Nano.5V, J10.pin2
  N27: Arduino_Nano.A7, J10.pin3
  N28: Arduino_Nano.A6, J10.pin4
  N29: Arduino_Nano.A3, J9.pin1
  N30: Arduino_Nano.A2, J9.pin2
  N31: Arduino_Nano.A1, J9.pin3
  N32: Arduino_Nano.D13/SCK, J8.pin1
  N33: RR2-5K.Pin_1, Arduino_Nano_2.3V3
  N34: J6.pin1, Arduino_Nano_2.A3
  N35: J6.pin2, Arduino_Nano_2.A2
  N36: J6.pin3, Arduino_Nano_2.A1
  N37: J7.pin1, Arduino_Nano_2.D13/SCK
  N38: J12.pin1, Arduino_Nano_2.D1/TX
  N39: J12.pin2, Arduino_Nano_2.D0/RX
  N40: J12.pin3, J5.pin1, Arduino_Nano_2.RESET
  N41: J12.pin5, Arduino_Nano_2.D2
  N42: J12.pin6, Arduino_Nano_2.D3, J3.pin1
  N43: J12.pin7, Arduino_Nano_2.D4, J3.pin2
  N44: J12.pin8, Arduino_Nano_2.D5, J3.pin3
  N45: J12.pin9, Arduino_Nano_2.D6, J3.pin4
  N46: J12.pin10, Arduino_Nano_2.D7, J3.pin5
  N47: J12.pin11, Arduino_Nano_2.D8, J3.pin6
  N48: J12.pin12, Arduino_Nano_2.D9, J3.pin7
  N49: J12.pin13, Arduino_Nano_2.D10, J3.pin8
  N50: J12.pin14, Arduino_Nano_2.D11/MOSI
  N51: J12.pin15, Arduino_Nano_2.D12/MISO
  N52: J5.pin2, Arduino_Nano_2.5V
  N53: J5.pin3, Arduino_Nano_2.A7
  N54: J5.pin4, Arduino_Nano_2.A6

notes:
  Power
  I2C Bus
  +5V
  GND
  SDA
  SCL
  VU Analyser, Takes audio input and sends data to master via I2C.  NOTE: Ensure Slave Addresses are different (8&9) 
  VIN
  TX
  RX
  SPARES
  Audio In
  100K
  100nF
  4.7K
  VU STEREO ANALYSER
  VU Stereo Analyser - Stephen Sweeney
  5V BOARD
  DO NOT CONNECT TO 3.3V SBC
  VOLTAGE LOGIC CONVERTERS
  WITHOUT APPROPRIATE CONTROL
  WARNING
  3 4 5 6 7 8 9 10
